// Logisim project B1.circ as structural Verilog
module _2 (
);

  // NAND_Gate nand_1 is placed but not wired
endmodule

module _2_C (
  input  A,
  input  B,
  output C
);

  wire nand_1_out, nand_2_out;

  nand nand_1 (nand_1_out, A, A);
  nand nand_2 (nand_2_out, B, B);
  nand nand_3 (C, nand_1_out, nand_2_out);
endmodule

module _3 (
  input  A,
  output B
);

  nor nor_1 (B, A, A);
endmodule

module _4 (
  input  A,
  input  B,
  input  C,
  output D
);

  wire nand_1_out, not_1_out;

  nand nand_1 (nand_1_out, A, B);
  not not_1 (not_1_out, C);
  or or_1 (D, nand_1_out, not_1_out);
endmodule

module _4_B (
  input  A,
  input  B,
  input  C,
  output D
);

  wire and_1_out, nor_1_out;

  nor nor_1 (nor_1_out, A, B);
  and and_1 (and_1_out, B, C);
  or or_1 (D, nor_1_out, and_1_out);
endmodule

module _6 (
  input  A,
  input  B,
  input  C,
  output D
);

  wire not_1_out, or_1_out;

  or or_1 (or_1_out, A, B);
  not not_1 (not_1_out, C);
  and and_1 (D, or_1_out, not_1_out);
endmodule

module _7 (
  input  A,
  input  B,
  input  C,
  output D
);

  and and_1 (D, A, B, C);
endmodule

module _7_2 (
  input  A,
  input  B,
  input  C,
  output D
);

  or or_1 (D, A, B, C);
endmodule

module _8_A (
  input  A,
  input  B,
  input  C,
  output D
);

  wire and_1_out;

  and and_1 (and_1_out, A, B);
  or or_1 (D, and_1_out, C);
endmodule

module _8_B (
  input  A,
  input  B,
  input  C,
  input  D,
  input  E,
  input  F,
  output G
);

  wire and_1_out, nand_1_out, nand_2_out;

  nand nand_1 (nand_1_out, A, B);
  and and_1 (and_1_out, C, D);
  nand nand_2 (nand_2_out, E, F);
  or or_1 (G, nand_1_out, and_1_out, nand_2_out);
endmodule

module _8_C (
  input  A,
  input  B,
  input  C,
  output D
);

  wire not_1_out, or_1_out, or_2_out, or_3_out;

  not not_1 (not_1_out, A);
  or or_1 (or_1_out, A, C);
  or or_2 (or_2_out, not_1_out, B);
  or or_3 (or_3_out, B, C);
  and and_1 (D, or_2_out, or_1_out, or_3_out);
endmodule
